// Logisim project 8_bit_bus.circ as structural Verilog: 1 circuit, main circuit main
module main (
  input  in_1
);

  wire and_1_out, and_3_out, and_4_out, and_5_out, b0, b1, b2, b3, b4, b5, b6, b7, button_1_out, Ck_Y, Ck_Z,
       CkR0, CkR1, CkR2, CkR3, CkR4, CkR5, CkR6, CkR7, Clear, clock_1_out, d_ff_1_q, En_Mem_to_Bus, En_Z,
       EnR0, EnR1, EnR2, EnR3, EnR4, EnR5, EnR6, EnR7, func_sel_0, func_sel_1, nor_1_out, not_1_out,
       not_2_out;
  wire [3:0] controlled_buffer_1_out, controlled_buffer_1_out_2;
  wire [3:3] hx7;
  wire [7:0] adder_1_out, and_2_out, counter_1_q, multiplexer_1_out, multiplier_1_out, or_1_out, R0, R1, R2,
       R3, R4, R5, R6, R7, Y, Z;

  LED led_1 (.in(En_Mem_to_Bus));
  assign {controlled_buffer_1_out_2, controlled_buffer_1_out} = En_Mem_to_Bus ? {b7, b6, b5, b4, b3, b2, b1, b0} : 8'bz;  // Controlled_Buffer controlled_buffer_1
  Clock clock_1 (.out(clock_1_out));
  LED led_2 (.in(Clear));
  assign {controlled_buffer_1_out_2, controlled_buffer_1_out} = EnR0 ? R0 : 8'bz;  // Controlled_Buffer controlled_buffer_2
  Register register_1 (
    .D({controlled_buffer_1_out_2, controlled_buffer_1_out}), .Q(R0), .clk(CkR0), .clr(Clear));  // open: en
  LED led_3 (.in(EnR0));
  LED led_4 (.in(CkR0));
  DotMatrix #(.inputtype("row"), .matrixcols(8), .matrixrows(1), .dotshape("circle")) dotmatrix_1 (.row0({b7, b6, b5, b4, b3, b2, b1, b0}));
  D_Flip_Flop d_ff_1 (.Q(d_ff_1_q), .preset(button_1_out), .reset(hx7[3]));  // open: clk, D, Qn, en
  Button button_1 (.out(button_1_out));
  LED led_5 (.in(and_1_out));
  and and_1 (and_1_out, d_ff_1_q, clock_1_out, in_1);
  LED led_6 (.in(CkR1));
  assign {controlled_buffer_1_out_2, controlled_buffer_1_out} = EnR1 ? R1 : 8'bz;  // Controlled_Buffer controlled_buffer_3
  Register register_2 (
    .D({controlled_buffer_1_out_2, controlled_buffer_1_out}), .Q(R1), .clk(CkR1), .clr(Clear));  // open: en
  LED led_7 (.in(EnR1));
  LED led_8 (.in(Ck_Y));
  Counter #(.ongoal("continue")) counter_1 (
    .count(1'b1), .Q(counter_1_q), .clk(and_1_out));  // open: load, D, carry, clr
  LED led_9 (.in(hx7[3]));
  assign {controlled_buffer_1_out_2, controlled_buffer_1_out} = EnR2 ? R2 : 8'bz;  // Controlled_Buffer controlled_buffer_4
  Register register_3 (
    .D({controlled_buffer_1_out_2, controlled_buffer_1_out}), .Q(R2), .clk(CkR2), .clr(Clear));  // open: en
  LED led_10 (.in(EnR2));
  LED led_11 (.in(CkR2));
  Register register_4 (
    .D({controlled_buffer_1_out_2, controlled_buffer_1_out}), .en(1'b1), .Q(Y), .clk(Ck_Y));  // open: clr
  Hex_Digit_Display hex_digit_display_1 (.value(counter_1_q[7:4]));  // open: dp
  Hex_Digit_Display hex_digit_display_2 (.value(counter_1_q[3:0]));  // open: dp
  Register register_5 (
    .D({controlled_buffer_1_out_2, controlled_buffer_1_out}), .Q(R3), .clk(CkR3), .clr(Clear));  // open: en
  LED led_12 (.in(CkR3));
  Adder adder_1 (
    .a(Y), .b({controlled_buffer_1_out_2, controlled_buffer_1_out}), .out(adder_1_out), .cin(1'b0));  // open: cout
  Multiplier multiplier_1 (
    .a(Y), .b({controlled_buffer_1_out_2, controlled_buffer_1_out}), .out(multiplier_1_out), .cin({8{1'b0}}));  // open: cout
  assign and_2_out = Y & {controlled_buffer_1_out_2, controlled_buffer_1_out};  // AND_Gate and_2, 8 bits wide
  assign or_1_out = Y | {controlled_buffer_1_out_2, controlled_buffer_1_out};  // OR_Gate or_1, 8 bits wide
  assign {controlled_buffer_1_out_2, controlled_buffer_1_out} = EnR3 ? R3 : 8'bz;  // Controlled_Buffer controlled_buffer_5
  LED led_13 (.in(CkR4));
  LED led_14 (.in(EnR3));
  Multiplexer #(.select(2), .width(8), .enable("false")) multiplexer_1 (
    .in0(adder_1_out), .in1(multiplier_1_out), .in2(and_2_out), .in3(or_1_out), .out(multiplexer_1_out),
    .sel({func_sel_1, func_sel_0}));
  LED led_15 (.in(func_sel_0));
  LED led_16 (.in(func_sel_1));
  ROM #(.dataWidth(32)) rom_1 (
    .addr(counter_1_q),
    .data({hx7[3], func_sel_1, func_sel_0, Clear, En_Mem_to_Bus, En_Z, Ck_Z, Ck_Y, b7, b6, b5, b4, b3, b2, b1, b0, CkR7, CkR6, CkR5, CkR4, CkR3, CkR2, CkR1, CkR0, EnR7, EnR6, EnR5, EnR4, EnR3, EnR2, EnR1, EnR0}));  // open: sel
  Hex_Digit_Display hex_digit_display_3 (.value({hx7[3], func_sel_1, func_sel_0, Clear}));  // open: dp
  assign {controlled_buffer_1_out_2, controlled_buffer_1_out} = EnR4 ? R4 : 8'bz;  // Controlled_Buffer controlled_buffer_6
  Register register_6 (
    .D({controlled_buffer_1_out_2, controlled_buffer_1_out}), .Q(R4), .clk(CkR4), .clr(Clear));  // open: en
  LED led_17 (.in(EnR4));
  Register register_7 (.D(multiplexer_1_out), .en(1'b1), .Q(Z), .clk(Ck_Z));  // open: clr
  LED led_18 (.in(Ck_Z));
  Hex_Digit_Display hex_digit_display_4 (.value({b7, b6, b5, b4}));  // open: dp
  Hex_Digit_Display hex_digit_display_5 (.value({En_Mem_to_Bus, En_Z, Ck_Z, Ck_Y}));  // open: dp
  assign {controlled_buffer_1_out_2, controlled_buffer_1_out} = EnR5 ? R5 : 8'bz;  // Controlled_Buffer controlled_buffer_7
  Register register_8 (
    .D({controlled_buffer_1_out_2, controlled_buffer_1_out}), .Q(R5), .clk(CkR5), .clr(Clear));  // open: en
  LED led_19 (.in(CkR5));
  LED led_20 (.in(EnR5));
  Hex_Digit_Display hex_digit_display_6 (.value(Z[7:4]));  // open: dp
  Hex_Digit_Display hex_digit_display_7 (.value({CkR7, CkR6, CkR5, CkR4}));  // open: dp
  Hex_Digit_Display hex_digit_display_8 (.value({b3, b2, b1, b0}));  // open: dp
  Register register_9 (
    .D({controlled_buffer_1_out_2, controlled_buffer_1_out}), .Q(R6), .clk(CkR6), .clr(Clear));  // open: en
  LED led_21 (.in(CkR6));
  Hex_Digit_Display hex_digit_display_9 (.value(Z[3:0]));  // open: dp
  Hex_Digit_Display hex_digit_display_10 (.value({EnR7, EnR6, EnR5, EnR4}));  // open: dp
  Hex_Digit_Display hex_digit_display_11 (.value({CkR3, CkR2, CkR1, CkR0}));  // open: dp
  assign {controlled_buffer_1_out_2, controlled_buffer_1_out} = EnR6 ? R6 : 8'bz;  // Controlled_Buffer controlled_buffer_8
  LED led_22 (.in(EnR6));
  LED led_23 (.in(CkR7));
  Hex_Digit_Display hex_digit_display_12 (.value({EnR3, EnR2, EnR1, EnR0}));  // open: dp
  assign {controlled_buffer_1_out_2, controlled_buffer_1_out} = EnR7 ? R7 : 8'bz;  // Controlled_Buffer controlled_buffer_9
  Register register_10 (
    .D({controlled_buffer_1_out_2, controlled_buffer_1_out}), .Q(R7), .clk(CkR7), .clr(Clear));  // open: en
  LED led_24 (.in(EnR7));
  LED led_25 (.in(nor_1_out));
  nor nor_1 (nor_1_out, func_sel_0, func_sel_1);
  and and_3 (and_3_out, func_sel_0, not_1_out);
  LED led_26 (.in(and_3_out));
  not not_1 (not_1_out, func_sel_1);
  not not_2 (not_2_out, func_sel_0);
  and and_4 (and_4_out, not_2_out, func_sel_1);
  LED led_27 (.in(and_4_out));
  assign {controlled_buffer_1_out_2, controlled_buffer_1_out} = En_Z ? Z : 8'bz;  // Controlled_Buffer controlled_buffer_10
  LED led_28 (.in(En_Z));
  Hex_Digit_Display hex_digit_display_13 (.value(controlled_buffer_1_out_2));  // open: dp
  and and_5 (and_5_out, func_sel_0, func_sel_1);
  LED led_29 (.in(and_5_out));
  Hex_Digit_Display hex_digit_display_14 (.value(controlled_buffer_1_out));  // open: dp
  DotMatrix #(.inputtype("row"), .matrixcols(8), .matrixrows(8), .dotshape("circle")) dotmatrix_2 (
    .row0(R7), .row1(R6), .row2(R5), .row3(R4), .row4(R3), .row5(R2), .row6(R1), .row7(R0));
  DotMatrix #(.inputtype("row"), .matrixcols(8), .matrixrows(2), .dotshape("circle")) dotmatrix_3 (.row0(Y), .row1(Z));

  // Other names for the same wires on the sheet: hx0[3:0] = {EnR3, EnR2, EnR1, EnR0};
  //   hx1[3:0] = {EnR7, EnR6, EnR5, EnR4}; hx2[3:0] = {CkR3, CkR2, CkR1, CkR0}; hx3[3:0] = {CkR7, CkR6, CkR5, CkR4};
  //   hx4[3:0] = {b3, b2, b1, b0}; hx5[3:0] = {b7, b6, b5, b4}; hx6[3:0] = {En_Mem_to_Bus, En_Z, Ck_Z, Ck_Y};
  //   hx7[2:0] = {func_sel_1, func_sel_0, Clear}; STOP = hx7[3]

  // Notes on the sheet:
  //   Start
  //   Turn ON
  //   Y-->
  //   Assignment 5
  //   Michael Bonilla
  //   MEMORY
  //   Z-->
  //   ADD 00
  //   MUL 01
  //   AND 10
  //   OR 11
  //   MICRO PROGRAM
  //   contents of rom_1 (hex, n*v repeats v):
  //   0 8040000 8040100 804000 4a04000 400000 200 1080000 2 2000002 4000000 4000400 68aa0000 68aa0800
  //   68cc0000 68cc1000 60000008 61000008 60000010 62000010 4000000 4002000 80000000
  //   CSCI 155
  //   ADD
  //   MUL
  //   AND
  //   8
  //   /
  //   <-- CURRENT CONTROL WORD
  //   OR
  //   CURRENT ACTION
  //   Register Contents
  //   7
  //   BITs
  //   R7
  //   R6
  //   R5
  //   R4
  //   R3
  //   R2
  //   R1
  //   R0
  //   0
  //   Y
  //   Z
endmodule
