// Logisim project First.circ as structural Verilog: 1 circuit, main circuit main
module main (
  input  in_1
);

  wire I_O_out, nand_1_out, nand_2_out, nand_3_out, nand_4_out, nand_5_out, nand_6_out, not_1_out, not_2_out;

  Button I_O (.out(I_O_out));
  Button I_O_2 (.out(in_1));
  LED led_1 (.in(in_1));
  not not_1 (not_1_out, I_O_out);
  not not_2 (not_2_out, I_O_out);
  LED led_2 (.in(in_1));
  Clock clock_1 ();  // open: out
  not nand_1 (nand_1_out, in_1);  // NAND_Gate
  not nand_2 (nand_2_out, in_1);  // NAND_Gate
  nand nand_3 (nand_3_out, not_1_out, not_1_out, not_1_out);
  nand nand_4 (nand_4_out, not_2_out, not_2_out);
  LED led_3 (.in(nand_5_out));
  nand nand_5 (nand_5_out, nand_1_out, nand_1_out, nand_6_out);
  nand nand_6 (nand_6_out, nand_5_out, nand_5_out, nand_2_out);
  LED led_4 (.in(nand_6_out));
  LED led_5 (.in(nand_3_out));
  LED led_6 (.in(nand_4_out));

  // Notes on the sheet:
  //   S=0
  //   R=0
  //   D-Type
endmodule
