// Logisim project Logisim assignment 1.circ as structural Verilog: 1 circuit, main circuit main
module main (
  input  in_1,
  input  in_2,
  input  in_3,
  input  in_4,
  input  A,
  input  B,
  input  C_in
);

  wire and_1_out, and_2_out, and_3_out, and_4_out, and_5_out, and_6_out, and_7_out, and_8_out, and_9_out,
       and_10_out, and_11_out, and_12_out, and_13_out, and_14_out, and_15_out, and_16_out, and_17_out,
       and_18_out, clock_1_out, not_1_out, not_2_out, not_3_out, not_4_out, or_1_out, xnor_1_out, xor_1_out;

  LED led_1 (.in(in_1));
  not not_1 (not_1_out, in_1);
  Clock clock_1 (.out(clock_1_out));
  Button I_O (.out(clock_1_out));
  and and_1 (and_1_out, in_1, clock_1_out);
  and and_2 (and_2_out, not_1_out, clock_1_out);
  and and_3 (and_3_out, and_1_out, and_4_out);
  and and_4 (and_4_out, and_3_out, and_2_out);
  LED led_2 (.in(A));
  LED led_3 (.in(and_3_out));
  LED led_4 (.in(and_4_out));
  not not_2 (not_2_out, in_2);
  Clock clock_2 (.out(clock_1_out));
  LED led_5 (.in(xnor_1_out));
  xnor xnor_1 (xnor_1_out, A, B);
  LED led_6 (.in(in_2));
  LED led_7 (.in(in_4));
  not not_3 (not_3_out, in_4);
  Clock clock_3 (.out(clock_1_out));
  xor xor_1 (xor_1_out, xnor_1_out, C_in);
  LED led_8 (.in(and_5_out));
  and and_5 (and_5_out, C_in, xnor_1_out);
  and and_6 (and_6_out, B, A);
  LED led_9 (.in(and_6_out));
  and and_7 (and_7_out, in_2, clock_1_out);
  and and_8 (and_8_out, not_2_out, clock_1_out);
  and and_9 (and_9_out, in_4, clock_1_out);
  and and_10 (and_10_out, not_3_out, clock_1_out);
  LED led_10 (.in(xor_1_out));
  LED led_11 (.in(or_1_out));
  or or_1 (or_1_out, and_5_out, and_6_out);
  LED led_12 (.in(and_11_out));
  and and_11 (and_11_out, and_7_out, and_12_out);
  and and_12 (and_12_out, and_11_out, and_8_out);
  and and_13 (and_13_out, and_9_out, and_14_out);
  and and_14 (and_14_out, and_13_out, and_10_out);
  LED led_13 (.in(and_12_out));
  LED led_14 (.in(and_13_out));
  LED led_15 (.in(and_14_out));
  LED led_16 (.in(in_3));
  not not_4 (not_4_out, in_3);
  Clock clock_4 (.out(clock_1_out));
  and and_15 (and_15_out, in_3, clock_1_out);
  and and_16 (and_16_out, not_4_out, clock_1_out);
  and and_17 (and_17_out, and_15_out, and_18_out);
  and and_18 (and_18_out, and_17_out, and_16_out);
  LED led_17 (.in(and_17_out));
  LED led_18 (.in(and_18_out));

  // Notes on the sheet:
  //   S
  //   C_out
  //   Michael Bonilla  
  //   CSCI 155
  //   Assignment 1
  //   10/10/16
endmodule
