// Logisim project Logisim assignment 2.circ as structural Verilog: 1 circuit, main circuit main
module main (
  input  [7:0] in_1
);

  wire button_1_out, button_2_out;
  wire [7:0] adder_1_out, controlled_inverter_1_out, counter_1_q, counter_2_q;

  LED led_1 (.in(counter_2_q[7]));
  Counter counter_1 (.D(in_1), .Q(counter_1_q), .clr(button_1_out));  // open: load, count, carry, clk
  Button button_1 (.out(button_1_out));
  Button button_2 (.out(button_2_out));
  LED led_2 (.in(counter_2_q[5]));
  LED led_3 (.in(counter_2_q[6]));
  Controlled_Inverter #(.width(8)) controlled_inverter_1 (
    .in(counter_1_q), .out(controlled_inverter_1_out));  // open: en
  Adder adder_1 (.a(controlled_inverter_1_out), .b({8{1'b0}}), .out(adder_1_out), .cin(1'b1));  // open: cout
  Counter counter_2 (.D(adder_1_out), .Q(counter_2_q), .clr(button_2_out));  // open: load, count, carry, clk
  LED led_4 (.in(counter_2_q[3]));
  LED led_5 (.in(counter_2_q[4]));
  LED led_6 (.in(counter_2_q[2]));
  LED led_7 (.in(counter_2_q[1]));
  LED led_8 (.in(counter_2_q[0]));
  Hex_Digit_Display hex_digit_display_1 (.value(counter_2_q[3:0]));  // open: dp
  Hex_Digit_Display hex_digit_display_2 (.value(counter_2_q[7:4]));  // open: dp

  // Notes on the sheet:
  //   Michael Bonilla
  //   CSCI 155 
  //   10/18/2016
  //   Assignment 2
endmodule
