// Logisim project Transfer.circ as structural Verilog: 1 circuit, main circuit main
module main (
);

  wire undriven, undriven_2;
  wire [7:0] I_O_2_out, I_O_3_out, I_O_4_out, I_O_out, register_1_q, register_2_q, register_3_q, register_4_q;

  Button I_O (.out(I_O_out[0]));
  Button I_O_2 (.out(I_O_2_out[0]));
  Button I_O_3 (.out(I_O_3_out[0]));
  Button I_O_4 (.out(I_O_4_out[0]));
  Register register_1 (.D(I_O_out), .Q(register_1_q));  // open: en, clk, clr
  LED led_1 (.in(undriven));
  assign I_O_out[0] = undriven ? register_1_q[0] : 1'bz;  // Controlled_Buffer controlled_buffer_1
  Register register_2 (.D(I_O_2_out), .Q(register_2_q));  // open: en, clk, clr
  assign I_O_2_out[0] = undriven_2 ? register_2_q[0] : 1'bz;  // Controlled_Buffer controlled_buffer_2
  Register register_3 (.D(I_O_3_out), .Q(register_3_q));  // open: en, clk, clr
  assign I_O_3_out[0] = undriven_2 ? register_3_q[0] : 1'bz;  // Controlled_Buffer controlled_buffer_3
  Register register_4 (.D(I_O_4_out), .Q(register_4_q));  // open: en, clk, clr
  assign I_O_4_out[0] = undriven_2 ? register_4_q[0] : 1'bz;  // Controlled_Buffer controlled_buffer_4
  // Pins of 1 and 8 bits meet at I_O_2_out
  // Pins of 1 and 8 bits meet at I_O_4_out
  // Pins of 1 and 8 bits meet at register_4_q
  // Pins of 1 and 8 bits meet at I_O_3_out
  // Pins of 1 and 8 bits meet at register_3_q
  // Pins of 1 and 8 bits meet at I_O_out
  // Pins of 1 and 8 bits meet at register_1_q
  // Pins of 1 and 8 bits meet at register_2_q
endmodule
